// Logisim project COMPUTER.circ as structural Verilog
module NAND_Gate (
  input  A,
  input  B
);

  wire nand_1_out;

  nand nand_1 (nand_1_out, A, B);
  LED led_1 (.in(nand_1_out));
endmodule

module NOT_Gate (
  input  A,
  output Q
);

  nand nand_1 (Q, A, A);
endmodule
